// Logisim project sha94_proj2.circ as structural Verilog: 6 circuits, main circuit main
module main (
  output out_1
);

  wire ALUSrc, beq, bge, blt, bne, button_1_out, clk, clock_1_out, DispWE, Halt, jr, jump, MemWrite, put2,
       RegWrite;
  wire [1:0] RegDataSrc;
  wire [2:0] ALU_Op, rd, rs, rt;
  wire [3:0] display_1_out_6, display_1_out_7, display_1_out_8, display_1_out_9;
  wire [7:0] ALU_Out, B, imm, mem_out, PC_1, pc_2_pc_output, Reg_Data_In, Reg_Data_Out_1, Reg_Data_Out_2;
  wire [19:0] rom_1_data;

  Clock clock_1 (.out(clock_1_out));
  or or_1 (clk, clock_1_out, button_1_out);
  Button button_1 (.out(button_1_out));
  LED led_1 (.in(Halt));
  Hex_Digit_Display hex_digit_display_1 (.value(display_1_out_6));  // open: dp
  Display display_1 (
    .CLK(clk), .WE(DispWE), .put2(put2), .Data_Lo(Reg_Data_Out_1), .Data_High(Reg_Data_Out_2),
    .out_6(display_1_out_6), .out_7(display_1_out_7), .out_8(display_1_out_8), .out_9(display_1_out_9));
  Multiplexer #(.select(2), .width(8)) multiplexer_1 (
    .in0(ALU_Out), .in1(mem_out), .in2(imm), .in3(PC_1), .out(Reg_Data_In), .sel(RegDataSrc));  // open: en
  Register_File register_file_1 (
    .in_1(clk), .Reg_Data_In(Reg_Data_In), .WE(RegWrite), .rd(rd), .rs(rs), .rt(rt),
    .Reg_Data_Out_1(Reg_Data_Out_1), .Reg_Data_Out_2(Reg_Data_Out_2));
  // Probe on ALU_Out
  // Probe on B
  // Probe on ALU_Op
  Hex_Digit_Display hex_digit_display_2 (.value(display_1_out_8));  // open: dp
  Hex_Digit_Display hex_digit_display_3 (.value(display_1_out_7));  // open: dp
  Hex_Digit_Display hex_digit_display_4 (.value(display_1_out_9));  // open: dp
  // Probe on Reg_Data_Out_1
  // Probe on Reg_Data_Out_2
  // Probe on Reg_Data_In
  // Probe on rd
  // Probe on rs
  // Probe on rt
  // Probe on pc_2_pc_output
  PC pc_2 (
    .Halt(Halt), .CLK(clk), .offset(imm), .Jump(jump), .Reg_Data_Out1(Reg_Data_Out_1),
    .Reg_Data_Out2(Reg_Data_Out_2), .in_7(blt), .in_8(bge), .in_9(beq), .in_10(bne), .in_11(jr),
    .PC_Output(pc_2_pc_output), .PC_1(PC_1));
  Multiplexer #(.width(8)) multiplexer_2 (.in0(Reg_Data_Out_2), .in1(imm), .out(B), .sel(ALUSrc));  // open: en
  // Probe on RegDataSrc
  // Probe on RegWrite
  // Probe on ALUSrc
  // Probe on MemWrite
  // Probe on DispWE
  RAM #(.bus("separate")) ram_1 (
    .addr(ALU_Out), .din(Reg_Data_Out_2), .data(mem_out), .str(MemWrite), .clk(clk));  // open: sel, ld, clr
  ROM #(.dataWidth(20)) rom_1 (.addr(pc_2_pc_output), .data(rom_1_data));  // open: sel
  // Probe on blt
  // Probe on bge
  // Probe on beq
  // Probe on bne
  Control control_1 (
    .ROM_Output(rom_1_data), .out_2(out_1), .out_3(Halt), .out_4(ALU_Op), .out_5(RegWrite), .out_6(DispWE),
    .out_7(put2), .out_8(RegDataSrc), .out_9(rd), .out_10(rs), .out_11(rt), .out_12(imm), .out_13(MemWrite),
    .out_14(ALUSrc), .out_15(jump), .out_16(blt), .out_17(bge), .out_18(beq), .out_19(bne), .out_20(jr));
  ALU alu_1 (.A(Reg_Data_Out_1), .B(B), .ALU_Op(ALU_Op), .ALU_Out(ALU_Out));

  // Other names for the same wires on the sheet: InstructionType = out_1

  // Notes on the sheet:
  //   Data Memory(word-addressed)
endmodule

module Display (
  input  CLK,
  input  WE,
  input  put2,
  input  [7:0] Data_Lo,
  input  [7:0] Data_High,
  output [3:0] out_6,
  output [3:0] out_7,
  output [3:0] out_8,
  output [3:0] out_9
);

  wire [15:0] bit_extender_1_out, multiplexer_1_out;

  assign bit_extender_1_out = {{8{1'b0}}, Data_Lo};  // Bit_Extender bit_extender_1
  Multiplexer #(.width(16)) multiplexer_1 (
    .in0(bit_extender_1_out), .in1({Data_High, Data_Lo}), .out(multiplexer_1_out), .sel(put2));  // open: en
  Register #(.width(16)) register_1 (
    .D(multiplexer_1_out), .en(WE), .Q({out_6, out_7, out_8, out_9}), .clk(CLK));  // open: clr

  // Other names for the same wires on the sheet: Digit3[3:0] = out_9; Digit2[3:0] = out_8; Digit1[3:0] = out_7;
  //   Digit0[3:0] = out_6
endmodule

module ALU (
  input  [7:0] A,
  input  [7:0] B,
  input  [2:0] ALU_Op,
  output [7:0] ALU_Out
);

  wire [2:0] bit_extender_1_out, bit_extender_2_out;
  wire [7:0] adder_1_out, and_1_out, not_1_p3, or_1_out, shifter_1_out, shifter_2_out, subtractor_1_out,
       xor_1_out;

  Bit_Extender #(.out_width(3)) bit_extender_1 (.in(B), .out(bit_extender_1_out));
  assign xor_1_out = A ^ B;  // XOR_Gate xor_1, 8 bits wide
  // NOT_Gate #(.width(8)) not_1: pin names not known; wires that end beside it: B, B, not_1_p3
  Shifter shifter_1 (.in(A), .\dist (bit_extender_1_out), .out(shifter_1_out));
  Bit_Extender #(.out_width(3)) bit_extender_2 (.in(B), .out(bit_extender_2_out));
  assign or_1_out = A | B;  // OR_Gate or_1, 8 bits wide
  Shifter #(.shift("lr")) shifter_2 (.in(A), .\dist (bit_extender_2_out), .out(shifter_2_out));
  assign and_1_out = A & B;  // AND_Gate and_1, 8 bits wide
  Adder adder_1 (.a(A), .b(B), .out(adder_1_out));  // open: cin, cout
  Subtractor subtractor_1 (.a(A), .b(B), .out(subtractor_1_out));  // open: bin, bout
  Multiplexer #(.select(3), .width(8)) multiplexer_1 (
    .in0(adder_1_out), .in1(subtractor_1_out), .in2(and_1_out), .in3(or_1_out), .in4(xor_1_out),
    .in5(not_1_p3), .in6(shifter_1_out), .in7(shifter_2_out), .out(ALU_Out), .sel(ALU_Op));  // open: en
endmodule

module Register_File (
  input  in_1,
  input  [7:0] Reg_Data_In,
  input  [2:0] rs,
  input  WE,
  input  [2:0] rd,
  input  [2:0] rt,
  output [7:0] Reg_Data_Out_1,
  output [7:0] Reg_Data_Out_2
);

  wire demultiplexer_1_out1, demultiplexer_1_out2, demultiplexer_1_out3, demultiplexer_1_out4,
       demultiplexer_1_out5, demultiplexer_1_out6, demultiplexer_1_out7;
  wire [7:0] register_1_q, register_2_q, register_3_q, register_4_q, register_5_q, register_6_q, register_7_q;

  Demultiplexer #(.select(3)) demultiplexer_1 (
    .out1(demultiplexer_1_out1), .out2(demultiplexer_1_out2), .out3(demultiplexer_1_out3),
    .out4(demultiplexer_1_out4), .out5(demultiplexer_1_out5), .out6(demultiplexer_1_out6),
    .out7(demultiplexer_1_out7), .in(WE), .sel(rd));  // open: out0, en
  Register register_1 (.D(Reg_Data_In), .en(demultiplexer_1_out1), .Q(register_1_q), .clk(in_1));  // open: clr
  Register register_2 (.D(Reg_Data_In), .en(demultiplexer_1_out2), .Q(register_2_q), .clk(in_1));  // open: clr
  Register register_3 (.D(Reg_Data_In), .en(demultiplexer_1_out3), .Q(register_3_q), .clk(in_1));  // open: clr
  Register register_4 (.D(Reg_Data_In), .en(demultiplexer_1_out4), .Q(register_4_q), .clk(in_1));  // open: clr
  Register register_5 (.D(Reg_Data_In), .en(demultiplexer_1_out5), .Q(register_5_q), .clk(in_1));  // open: clr
  Register register_6 (.D(Reg_Data_In), .en(demultiplexer_1_out6), .Q(register_6_q), .clk(in_1));  // open: clr
  Register register_7 (.D(Reg_Data_In), .en(demultiplexer_1_out7), .Q(register_7_q), .clk(in_1));  // open: clr
  // Multiplexer #(.select(3), .width(8)) multiplexer_1: pin names not known; wires that end beside it: {8{1'b0}}, register_1_q, register_2_q, register_3_q, register_4_q, register_5_q, register_6_q, register_7_q, rs, Reg_Data_Out_1
  Multiplexer #(.select(3), .width(8)) multiplexer_2 (
    .in0({8{1'b0}}), .in1(register_1_q), .in2(register_2_q), .in3(register_3_q), .in4(register_4_q),
    .in5(register_5_q), .in6(register_6_q), .in7(register_7_q), .out(Reg_Data_Out_2), .sel(rt));  // open: en

  // Other names for the same wires on the sheet: CLK = in_1
endmodule

module PC (
  input  Halt,
  input  CLK,
  input  [7:0] offset,
  input  Jump,
  input  [7:0] Reg_Data_Out1,
  input  [7:0] Reg_Data_Out2,
  input  in_7,
  input  in_8,
  input  in_9,
  input  in_10,
  input  in_11,
  output [7:0] PC_Output,
  output [7:0] PC_1
);

  wire and_1_out, and_2_out, and_3_out, and_4_out, Branch, comparator_1_eq, comparator_1_gt, comparator_2_eq,
       comparator_3_lt, not_1_p2, not_2_out, or_1_out;
  wire [7:0] multiplexer_1_out, multiplexer_2_out, multiplexer_3_out;

  Multiplexer #(.width(8)) multiplexer_1 (.in0(8'h1), .in1(offset), .out(multiplexer_1_out), .sel(Branch));  // open: en
  Adder adder_1 (.a(PC_Output), .b(multiplexer_1_out), .out(PC_1));  // open: cin, cout
  Multiplexer #(.width(8)) multiplexer_2 (.in0(PC_1), .in1(offset), .out(multiplexer_2_out), .sel(Jump));  // open: en
  Comparator comparator_1 (
    .a(Reg_Data_Out1), .b(Reg_Data_Out2), .gt(comparator_1_gt), .eq(comparator_1_eq));  // open: lt
  Comparator comparator_2 (.a(Reg_Data_Out1), .b(Reg_Data_Out2), .eq(comparator_2_eq));  // open: gt, lt
  Multiplexer #(.width(8)) multiplexer_3 (
    .in0(multiplexer_2_out), .in1(Reg_Data_Out1), .out(multiplexer_3_out), .sel(in_11));  // open: en
  Comparator comparator_3 (.a(Reg_Data_Out1), .b(Reg_Data_Out2), .lt(comparator_3_lt));  // open: gt, eq
  or or_1 (or_1_out, comparator_1_gt, comparator_1_eq);
  and and_1 (and_1_out, or_1_out, in_8);
  and and_2 (and_2_out, comparator_2_eq, in_9);
  // NOT_Gate not_1: pin names not known; wires that end beside it: comparator_2_eq, not_1_p2
  and and_3 (and_3_out, not_1_p2, in_10);
  not not_2 (not_2_out, Halt);
  and and_4 (and_4_out, comparator_3_lt, in_7);
  Register register_1 (.D(multiplexer_3_out), .en(not_2_out), .Q(PC_Output), .clk(CLK));  // open: clr
  or or_2 (Branch, and_4_out, and_1_out, and_2_out, and_3_out);

  // Other names for the same wires on the sheet: beq = in_9; bge = in_8; blt = in_7; bne = in_10; jr = in_11;
  //   REG_rs[7:0] = Reg_Data_Out1; REG_rt[7:0] = Reg_Data_Out2
endmodule

module Control (
  input  [19:0] ROM_Output,
  output out_2,
  output out_3,
  output [2:0] out_4,
  output out_5,
  output out_6,
  output out_7,
  output [1:0] out_8,
  output [2:0] out_9,
  output [2:0] out_10,
  output [2:0] out_11,
  output [7:0] out_12,
  output out_13,
  output out_14,
  output out_15,
  output out_16,
  output out_17,
  output out_18,
  output out_19,
  output out_20
);

  wire add, adi, And, ani, branch, j, jal, ld, li, \not , \or , or_2_out, or_3_out, or_4_out, or_5_out,
       or_6_out, or_7_out, ori, put, sbi, shl, shr, sli, sri, sub, undriven, undriven_2, undriven_3, \xor ,
       xri;
  wire [4:0] imm5;
  wire [7:0] bit_extender_1_out, bit_extender_2_out, imm8, multiplexer_1_out;
  wire [19:0] demultiplexer_2_out0, demultiplexer_2_out1;

  or or_1 (out_14, adi, sbi, ani, out_13, ori, ld, xri, sli, sri);
  Demultiplexer #(.select(5)) demultiplexer_1 (
    .out0(out_3), .out1(put), .out2(out_7), .out3(li), .out4(out_13), .out5(ld), .out6(add), .out7(sub),
    .out8(And), .out9(\or ), .out10(\xor ), .out11(\not ), .out12(shl), .out13(shr), .out14(adi),
    .out15(sbi), .out16(ani), .out17(ori), .out18(xri), .out19(sli), .out20(sri), .out21(j), .out22(out_16),
    .out23(out_17), .out24(out_18), .out25(out_19), .out26(jal), .out27(out_20), .in(1'b1),
    .sel(ROM_Output[18:14]));  // open: out28, out29, out30, out31, en
  assign bit_extender_1_out = {{3{1'b0}}, imm5};  // Bit_Extender bit_extender_1
  assign bit_extender_2_out = {{3{imm5[4]}}, imm5};  // Bit_Extender bit_extender_2
  or or_2 (or_2_out, sub, sbi);
  buf or_3 (or_3_out, undriven);  // OR_Gate
  or or_4 (or_4_out, undriven, undriven_2);
  or or_5 (or_5_out, undriven_2, undriven_3);
  buf or_6 (or_6_out, undriven_3);  // OR_Gate
  or or_7 (or_7_out, shr, sri);
  Multiplexer #(.width(8)) multiplexer_1 (
    .in0(bit_extender_1_out), .in1(bit_extender_2_out), .out(multiplexer_1_out), .sel(branch));  // open: en
  Multiplexer #(.width(8)) multiplexer_2 (
    .in0(multiplexer_1_out), .in1(imm8), .out(out_12), .sel(ROM_Output[19]));  // open: en
  Demultiplexer #(.width(20)) demultiplexer_2 (
    .out0({demultiplexer_2_out0[19:14], imm5, out_11, demultiplexer_2_out0[5:0]}),
    .out1({demultiplexer_2_out1[19:14], imm8, demultiplexer_2_out1[5:0]}), .in(ROM_Output),
    .sel(ROM_Output[19]));  // open: en
  Priority_Encoder priority_encoder_1 (
    .in0(1'b1), .in1(or_2_out), .in2(or_3_out), .in3(or_4_out), .in4(or_5_out), .in5(\not ), .in6(or_6_out),
    .in7(or_7_out), .out(out_4));  // open: en_in, gs, en_out
  or or_8 (out_5, ld, shr, add, sub, And, \or , \xor , \not , shl, adi, sbi, ani, ori, xri, sli, sri, li, jal);
  or or_9 (out_6, put, out_7);
  Priority_Encoder #(.select(2)) priority_encoder_2 (
    .in0(1'b1), .in1(ld), .in2(li), .in3(jal), .out(out_8));  // open: gs, en_out, en_in
  or or_10 (out_15, j, jal);
  or or_11 (branch, out_16, out_17, out_18, out_19);

  assign out_2 = ROM_Output[19];
  assign out_9 = ROM_Output[2:0];
  assign out_10 = ROM_Output[5:3];

  // Other names for the same wires on the sheet: rt[2:0] = out_11; ALUOp[2:0] = out_4; ALUSrc = out_14; beq = out_18;
  //   bge = out_17; blt = out_16; bne = out_19; Ctrl_Input[19:0] = ROM_Output; rd[2:0] = ROM_Output[2:0];
  //   rs[2:0] = ROM_Output[5:3]; Opcode[4:0] = ROM_Output[18:14]; InstructionType = ROM_Output[19]; DispWE = out_6;
  //   Halt = out_3; imm[7:0] = out_12; jr = out_20; jump = out_15; put2 = out_7; RegDataSrc[1:0] = out_8;
  //   RegWrite = out_5; MemWrite = out_13; st = out_13
endmodule
